// Logisim project processor.circ as structural Verilog: 6 circuits, main circuit MIPS32
module MIPS32 (
);

  wire clock_1_out;
  wire [31:0] A_q, B_2_q, B_q, ctrl_2_q, ctrl_q, D_2_q, D_q, ex_1_bout, ex_1_d, ex_1_target, id_1_a, id_1_b,
       id_1_ctrl_2, id_1_imm, id_1_pc_4out, if_1_ctrl, if_1_inst, if_1_pc_4, imm_q, M_q, mem_1_ctrlout,
       mem_1_dout, mem_1_m, PC_4_q, register_1_q, register_2_q, register_3_q, wb_1_ctrl_out, wb_1_wb;

  IF if_1 (.Clock(clock_1_out), .target(ex_1_target), .ctrl(if_1_ctrl), .inst(if_1_inst), .PC_4(if_1_pc_4));
  Register #(.width(32)) register_1 (.D(if_1_inst), .Q(register_1_q), .clk(clock_1_out));  // open: en, clr
  Register #(.width(32)) register_2 (.D(if_1_pc_4), .Q(register_2_q), .clk(clock_1_out));  // open: en, clr
  ID id_1 (
    .ctrl(wb_1_ctrl_out), .inst(register_1_q), .PC_4(register_2_q), .A(id_1_a), .B(id_1_b), .imm(id_1_imm),
    .PC_4out(id_1_pc_4out), .ctrl_2(id_1_ctrl_2), .wb(wb_1_wb), .Clock(clock_1_out));
  Register #(.width(32)) A (.D(id_1_a), .Q(A_q), .clk(clock_1_out), .clr(clock_1_out));  // open: en
  Register #(.width(32)) B (.D(id_1_b), .Q(B_q), .clk(clock_1_out));  // open: en, clr
  Register #(.width(32)) imm (.D(id_1_imm), .Q(imm_q), .clk(clock_1_out));  // open: en, clr
  Register #(.width(32)) PC_4 (.D(id_1_pc_4out), .Q(PC_4_q), .clk(clock_1_out));  // open: en, clr
  Register #(.width(32)) ctrl (.D(id_1_ctrl_2), .Q(ctrl_q), .clk(clock_1_out));  // open: en, clr
  EX ex_1 (
    .A(A_q), .B(B_q), .imm(imm_q), .PC_4(PC_4_q), .ctrl(ctrl_q), .target(ex_1_target), .D(ex_1_d),
    .Bout(ex_1_bout), .ctrlout(if_1_ctrl));
  Register #(.width(32)) D (.D(ex_1_d), .Q(D_q), .clk(clock_1_out));  // open: en, clr
  Register #(.width(32)) B_2 (.D(ex_1_bout), .Q(B_2_q), .clk(clock_1_out));  // open: en, clr
  Register #(.width(32)) ctrl_2 (.D(if_1_ctrl), .Q(ctrl_2_q), .clk(clock_1_out));  // open: en, clr
  Register #(.width(32)) D_2 (.D(mem_1_dout), .Q(D_2_q), .clk(clock_1_out));  // open: en, clr
  MEM mem_1 (
    .D(D_q), .B(B_2_q), .ctrl(ctrl_2_q), .Clock(clock_1_out), .Dout(mem_1_dout), .M(mem_1_m),
    .ctrlout(mem_1_ctrlout));
  Register #(.width(32)) M (.D(mem_1_m), .Q(M_q), .clk(clock_1_out));  // open: en, clr
  Register #(.width(32)) register_3 (.D(mem_1_ctrlout), .Q(register_3_q), .clk(clock_1_out));  // open: en, clr
  Clock clock_1 (.out(clock_1_out));
  WB wb_1 (.D(D_2_q), .M(M_q), .ctrl(register_3_q), .WB(wb_1_wb), .ctrl_out(wb_1_ctrl_out));
endmodule

module EX (
  input  [31:0] A,
  input  [31:0] B,
  input  [31:0] imm,
  input  [31:0] PC_4,
  input  [31:0] ctrl,
  output [31:0] target,
  output [31:0] D,
  output [31:0] Bout,
  output [31:0] ctrlout
);

  wire mips_alu_1_p1;
  wire [31:0] multiplexer_1_out;

  Multiplexer #(.width(32), .enable("false")) multiplexer_1 (.in0(B), .in1(imm), .out(multiplexer_1_out));  // open: sel
  // Mips_ALU mips_alu_1: pin names not known; wires that end beside it: mips_alu_1_p1, A, multiplexer_1_out, mips_alu_1_p1, D, target

  assign Bout = B;
  assign ctrlout = ctrl;
endmodule

module IF (
  input  [31:0] target,
  input  Clock,
  output [31:0] ctrl,
  output [31:0] inst,
  output [31:0] PC_4
);

  wire incrementer_1_p3;
  wire [31:0] incrementer_1_p5, multiplexer_1_out;

  Multiplexer #(.width(32), .enable("false")) multiplexer_1 (
    .in0({PC_4[31:2], 2'b00}), .in1(target), .out(multiplexer_1_out), .sel(incrementer_1_p3));
  // Incrementer incrementer_1: pin names not known; wires that end beside it: incrementer_1_p5[31:2], PC_4[31:2], incrementer_1_p3, ctrl, incrementer_1_p5
  Register #(.width(32)) register_1 (.D(multiplexer_1_out), .Q(incrementer_1_p5), .clk(Clock));  // open: en, clr
  // MIPSProgramROM mipsprogramrom_1: pin names not known; wires that end beside it: inst

  assign PC_4[1:0] = 2'b00;

  // Other names for the same wires on the sheet: tPC_4[31:2] = PC_4[31:2]
endmodule

module MEM (
  input  [31:0] D,
  input  [31:0] B,
  input  [31:0] ctrl,
  input  Clock,
  output [31:0] Dout,
  output [31:0] M,
  output [31:0] ctrlout
);

  // MIPS_RAM mips_ram_1: pin names not known; wires that end beside it: Clock

  assign ctrlout = ctrl;
  assign Dout = D;
  assign M = {32{1'b0}};
endmodule

module WB (
  input  [31:0] D,
  input  [31:0] M,
  input  [31:0] ctrl,
  output [31:0] WB,
  output [31:0] ctrl_out
);

  wire undriven;

  Multiplexer #(.width(32), .enable("false")) multiplexer_1 (.in0(D), .in1(M), .out(WB), .sel(undriven));

  assign ctrl_out = ctrl;
endmodule

module ID (
  input  [31:0] ctrl,
  input  [31:0] wb,
  input  [31:0] inst,
  input  [31:0] PC_4,
  input  Clock,
  output [31:0] A,
  output [31:0] B,
  output [31:0] imm,
  output [31:0] PC_4out,
  output [31:0] ctrl_2
);

  // RegisterFile registerfile_1: pin names not known; wires that end beside it: wb, Clock, ctrl, A, B
  Bit_Extender #(.in_width(16), .out_width(32), .\type ("sign")) bit_extender_1 (.out(imm));  // open: in

  assign PC_4out = PC_4;
endmodule
